# Fritzing sketch AR envelope generator (saved by Fritzing 0.9.2b)
breadboards: 1

parts:
  IC1 = IC, DIP package, 14 pins [chip_label=MCP]
  R1 = Rotary Potentiometer (Small) [maximum_resistance=100kΩ package=THT]
  R2 = Rotary Potentiometer (Small) [maximum_resistance=100kΩ package=THT]
  D1 = Rectifier Diode [part_number=1N4001 package="300 mil [THT]"]
  D2 = Rectifier Diode [part_number=1N4001 package="300 mil [THT]"]
  C1 = Ceramic Capacitor [capacitance=100nF package="100 mil [THT, multilayer]"]
  R3 = Resistor [tolerance=±5% resistance=100 package=THT]
  R4 = Resistor [tolerance=±5% resistance=100 package=THT]

nets:
  N1: IC1.pin1, IC1.pin2, R4.Pin_1
  N2: IC1.pin3, C1.1, R3.Pin_1
  N3: IC1.pin11, C1.0
  N4: R1.wiper, D2.anode
  N5: R1.leg2, R2.leg2
  N6: R2.wiper, D1.cathode
  N7: D1.anode, D2.cathode, R3.Pin_0

notes:
  ATTACK
  RELEASE
  ENV OUT
  GATE IN
  0V
  5V
  AR (Attack/Release) Envelope Generator:
  This simple, yet effective, envelope generator could be used wherever a simple envelope is needed. You can build four of those with just a quad op amp and few components. To rise the time constant , simply increase the capacitor value (here is a 100nF ceramic).
