# Fritzing sketch ataripunkconsole (saved by Fritzing 0.9.2b)
breadboards: 1

parts:
  U1 = 555 Timer [package="DIP8 [THT]"]
  U2 = 555 Timer [package="DIP8 [THT]"]
  R1 = Rotary Potentiometer (Small) [maximum_resistance=100kΩ package=THT]
  R2 = Rotary Potentiometer (Small) [maximum_resistance=100kΩ package=THT]
  C1 = Ceramic Capacitor [capacitance=100nF voltage=20V part_number=C! package="100 mil [THT, multilayer]"]
  C2 = Electrolytic Capacitor [capacitance=1µF voltage=6.3V package="100 mil [THT, electrolytic]"]
  R3 = Resistor [tolerance=±5% resistance=1k package=THT]
  R3_2 = Resistor [tolerance=±5% resistance=1k part_number=R1 package=THT]

nets:
  N1: U1.Ground, U1.Reset, U1.Vcc_Supply_Voltage, U2.Ground, U2.Reset, U2.Vcc_Supply_Voltage, R1.wiper, R1.leg2, R2.wiper, R2.leg2, C1.0, C2.-
  N2: U1.Trigger, U2.Output
  N3: U1.Threshold, U1.Discharge, R2.leg1, C2.+
  N4: U2.Trigger, U2.Threshold, C1.1, R3.Pin_0, R3_2.Pin_0
  N5: U2.Discharge, R1.leg1, R3.Pin_1, R3_2.Pin_1

notes:
  ATARI PUNK CONSOLE
  (firstly described in the book Siliconcepts by Forrest M.Mims)
  NS1nanosynth experimenter's kit
  OUTPUT
  FREQ
  PW
  0V
  5V
  Resistor is 1K
  Ceramic cap is 100nF
  Electrolytic cap is 1uF
