# Fritzing sketch cmosringmod (saved by Fritzing 0.9.2b)
breadboards: 1

parts:
  IC1 = IC, DIP package, 14 pins [chip_label=CD4011]
  R1 = Resistor [tolerance=±5% resistance=100 package=THT]

nets:
  N1: IC1.pin1, IC1.pin13
  N2: IC1.pin2, IC1.pin5
  N3: IC1.pin3, IC1.pin6, IC1.pin12
  N4: IC1.pin4, IC1.pin9
  N5: IC1.pin8, IC1.pin11
  N6: IC1.pin10, R1.Pin_1

notes:
  CMOS Ring Modulator:
  A simple, single chip, ring modulator for general purpose metallic sound generation!
  OUTPUT
  INPUT 1
  INPUT 2
  0V
  5V
