# Fritzing sketch envelope follower (saved by Fritzing 0.9.2b)
breadboards: 1

parts:
  IC1 = IC, DIP package, 14 pins [chip_label=MCP]
  R2 = Resistor [tolerance=±5% resistance=10k package=THT]
  R3 = Resistor [tolerance=±5% resistance=100k package=THT]
  C1 = Electrolytic Capacitor [capacitance=1µF package="100 mil [THT, electrolytic]"]
  R4 = Resistor [tolerance=±5% resistance=10k package=THT]
  R1 = Rotary Potentiometer (Small) [maximum_resistance=100kΩ package=THT]
  R5 = Resistor [tolerance=±5% resistance=100 package=THT]
  C2 = Electrolytic Capacitor [capacitance=1µF package="100 mil [THT, electrolytic]"]
  R6 = Resistor [tolerance=±5% resistance=10k package=THT]
  D1 = Rectifier Diode [part_number=1N4001 package="300 mil [THT]"]
  R7 = Resistor [tolerance=±5% resistance=10k package=THT]
  R8 = Resistor [tolerance=±5% resistance=10k package=THT]
  D2 = Rectifier Diode [part_number=1N4001 package="300 mil [THT]"]
  R9 = Resistor [tolerance=±5% resistance=100 package=THT]
  C3 = Electrolytic Capacitor [capacitance=10µF package="100 mil [THT, electrolytic]"]
  R10 = Resistor [tolerance=±5% resistance=10k package=THT]
  R11 = Resistor [tolerance=±5% resistance=1k package=THT]
  R12 = Resistor [tolerance=±5% resistance=100 package=THT]
  R13 = Resistor [tolerance=±5% resistance=1k package=THT]
  R14 = Resistor [tolerance=±5% resistance=1k package=THT]
  R15 = Resistor [tolerance=±5% resistance=1k package=THT]
  R16 = Resistor [tolerance=±5% resistance=100k package=THT]
  R17 = Resistor [tolerance=±5% resistance=1k package=THT]
  R18 = Resistor [tolerance=±5% resistance=100k package=THT]
  R19 = Resistor [tolerance=±5% resistance=100 package=THT]
  R20 = Resistor [tolerance=±5% resistance=1k package=THT]
  LED1 = LED - 3mm [color="Green (570nm)" package="3 mm [THT]"]

nets:
  N1: IC1.pin1, R1.wiper, R5.Pin_1, C2.+
  N2: IC1.pin2, R4.Pin_1, R1.leg1
  N3: IC1.pin3, R2.Pin_1, R3.Pin_0
  N4: IC1.pin4, R2.Pin_0, R3.Pin_1, R16.Pin_0
  N5: IC1.pin6, R6.Pin_1, R7.Pin_0, D2.anode
  N6: IC1.pin7, D1.anode
  N7: IC1.pin8, R18.Pin_0, R19.Pin_1, R20.Pin_0
  N8: IC1.pin9, R15.Pin_0, R16.Pin_1
  N9: IC1.pin10, R17.Pin_0, R18.Pin_1
  N10: IC1.pin11, C3.-, R10.Pin_1, R13.Pin_0, LED1.cathode
  N11: IC1.pin12, R9.Pin_1, C3.+, R10.Pin_0
  N12: IC1.pin13, R11.Pin_1
  N13: IC1.pin14, R11.Pin_0, R12.Pin_1, R17.Pin_1
  N14: C1.+, R4.Pin_0
  N15: C2.-, R6.Pin_0
  N16: D1.cathode, R8.Pin_1, D2.cathode, R9.Pin_0
  N17: R7.Pin_1, R8.Pin_0
  N18: R13.Pin_1, R14.Pin_1
  N19: R14.Pin_0, R15.Pin_1
  N20: R20.Pin_1, LED1.anode

notes:
  INPUT GAIN
  AUDIO IN
  AUDIO OUT
  0V
  5V
  ENVELOPE OUT
  GATE OUT
  Envelope Follower:
  The ENVELOPE output could be used as a CV to control filters (auto-wha) or other modules. The input gain stage is also useful to transform low-level signals (guitar, microphone, etc..) into modular range through the AUDIO OUT output. A GATE signal is also generated.
