# Fritzing sketch stepseq1 (saved by Fritzing 0.9.2b)
circuit board: 8.46667cm x 5.64444cm
breadboards: 1

parts:
  R1 = Rotary Potentiometer (Small) [maximum_resistance=100kΩ package=THT]
  R2 = Rotary Potentiometer (Small) [maximum_resistance=100kΩ package=THT]
  R3 = Rotary Potentiometer (Small) [maximum_resistance=100kΩ package=THT]
  R4 = Rotary Potentiometer (Small) [maximum_resistance=100kΩ package=THT]
  R5 = Rotary Potentiometer (Small) [maximum_resistance=100kΩ package=THT]
  R6 = Rotary Potentiometer (Small) [maximum_resistance=100kΩ package=THT]
  R7 = Rotary Potentiometer (Small) [maximum_resistance=100kΩ package=THT]
  R8 = Rotary Potentiometer (Small) [maximum_resistance=100kΩ package=THT]
  IC1 = IC, DIP package, 16 pins [chip_label=4017]
  D1 = Rectifier Diode [part_number=1N4001 package="300 mil [THT]"]
  D2 = Rectifier Diode [part_number=1N4001 package="300 mil [THT]"]
  D3 = Rectifier Diode [part_number=1N4001 package="300 mil [THT]"]
  D4 = Rectifier Diode [part_number=1N4001 package="300 mil [THT]"]
  D5 = Rectifier Diode [part_number=1N4001 package="300 mil [THT]"]
  D6 = Rectifier Diode [part_number=1N4001 package="300 mil [THT]"]
  D7 = Rectifier Diode [part_number=1N4001 package="300 mil [THT]"]
  D8 = Rectifier Diode [part_number=1N4001 package="300 mil [THT]"]

nets:
  N1: R1.leg1, IC1.pin3
  N2: R1.wiper, D8.anode
  N3: R1.leg2, R2.leg2, R3.leg2, R4.leg2, R5.leg2, R6.leg2, R7.leg2, R8.leg2, IC1.pin8, IC1.pin13
  N4: R2.leg1, IC1.pin2
  N5: R2.wiper, D7.anode
  N6: R3.leg1, IC1.pin4
  N7: R3.wiper, D6.anode
  N8: R4.leg1, IC1.pin7
  N9: R4.wiper, D5.anode
  N10: R5.leg1, IC1.pin10
  N11: R5.wiper, D4.anode
  N12: R6.leg1, IC1.pin1
  N13: R6.wiper, D3.anode
  N14: R7.leg1, IC1.pin5
  N15: R7.wiper, D2.anode
  N16: R8.leg1, IC1.pin6
  N17: R8.wiper, D1.anode
  N18: IC1.pin9, IC1.pin15
  clock: IC1.pin14
  5V: IC1.pin16
  cv out: D1.cathode, D2.cathode, D3.cathode, D4.cathode, D5.cathode, D6.cathode, D7.cathode, D8.cathode

notes:
  CLK IN
  CV OUT
  0V
  5V
  STEP 1
  STEP 2
  STEP 3
  STEP 4
  STEP 5
  STEP 6
  STEP 7
  STEP 8
  CD4017 based stepsequencer.
  The simplest sequencer out there. Just an IC, 8 pots, 8diodes. You can change the sequence length by connecting the pin 15(reset) with any of the output pins (3,2,4,7,10,1,5,6 for the first 8 stages) or put other two pots (on pins 9 and 11) to obtain a 10 steps sequencer!
  Credits to Baby10 sequencer by M. Hermann !!!
