# Fritzing sketch voltagecontrolledgate (saved by Fritzing 0.9.2b)
breadboards: 1

parts:
  U2 = 555 Timer [package="DIP8 [THT]"]
  C3 = Electrolytic Capacitor [capacitance=1µF voltage=6.3V package="100 mil [THT, electrolytic]"]
  R4 = Photocell (LDR) [package=THT]
  LED1 = LED - 3mm [color="Green (570nm)" part_number=LD1 package="3 mm [THT]"]
  R5 = Resistor [tolerance=±5% resistance=1k package=THT]

nets:
  N1: U2.Ground, C3.-, LED1.anode
  N2: U2.Reset, U2.Vcc_Supply_Voltage, R4.pin_1
  N3: U2.Threshold, U2.Discharge, C3.+, R4.pin_0
  N4: LED1.cathode, R5.Pin_1

notes:
  Voltage Controlled Gate
  a vactrol based trigger to gate processor. Try it with a sequencer and an ADSR!!!
  Increase control voltage to raise the length of the gate output!
  TRIG IN
  HOMEMADE VACTROL
  GATE OUT
  CV IN
  0V
  5V
